// Logisim project comp1.circ as structural Verilog: 2 circuits, main circuit main
module main (
);

  wire ADD, AI, ALO, and_1_out, and_2_out, and_3_out, and_4_out, AO, BI, BO, button_1_out, CE, clk,
       clock_1_out, CO, II, IO, JMP, MI, OI, RI, RO, SUB, switch_1_p2, switch_2_p2, switch_3_p2;
  wire [3:0] controlled_buffer_9_out, counter_1_q, MAR_q, OUTPUT_REG_q, OUTPUT_REG_q_2, register_1_q;
  wire [7:0] adder_1_out, ALU_IN_A, ALU_IN_B, BUS_1, controlled_buffer_5_out, dipswitch_1_sw1, ram_1_dout,
       subtractor_1_out;
  wire [23:16] pull_resistor_1_node;

  // Switch switch_1: pin names not known; wires that end beside it: 1'b1, switch_1_p2
  Clock clock_1 (.out(clock_1_out));
  Button button_1 (.out(button_1_out));
  Pull_Resistor pull_resistor_1 (.node({pull_resistor_1_node, IO, OI, CO, JMP, CE, RO, RI, MI, II, SUB, ADD, ALO, BO, BI, AO, AI}));
  CTRL ctrl_1 (
    .CLK(clk),
    .CONTROL_PINS({pull_resistor_1_node, IO, OI, CO, JMP, CE, RO, RI, MI, II, SUB, ADD, ALO, BO, BI, AO, AI}));  // open: IR_IN
  Pull_Resistor pull_resistor_2 (.node(switch_1_p2));
  and and_1 (and_1_out, switch_1_p2, clock_1_out);
  or or_1 (clk, and_1_out, button_1_out);
  // Switch switch_2: pin names not known; wires that end beside it: 1'b1, switch_2_p2
  DipSwitch dipswitch_1 (
    .sw1(dipswitch_1_sw1[0]), .sw2(dipswitch_1_sw1[1]), .sw3(dipswitch_1_sw1[2]), .sw4(dipswitch_1_sw1[3]),
    .sw5(dipswitch_1_sw1[4]), .sw6(dipswitch_1_sw1[5]), .sw7(dipswitch_1_sw1[6]), .sw8(dipswitch_1_sw1[7]));
  LedBar ledbar_1 (
    .led0(BUS_1[7]), .led1(BUS_1[6]), .led2(BUS_1[5]), .led3(BUS_1[4]), .led4(BUS_1[3]), .led5(BUS_1[2]),
    .led6(BUS_1[1]), .led7(BUS_1[0]));
  Register A_REG (.D(BUS_1), .en(AO), .clk(clk), .Q(ALU_IN_A));  // open: clr
  Register REG_B (.D(BUS_1), .en(BI), .clk(clk), .Q(ALU_IN_B));  // open: clr
  Pull_Resistor pull_resistor_3 (.node(switch_2_p2));
  assign BUS_1 = switch_2_p2 ? dipswitch_1_sw1 : 8'bz;  // Controlled_Buffer controlled_buffer_1
  // Probe on BUS_1
  Pull_Resistor pull_resistor_4 (.node(BUS_1));
  Pull_Resistor pull_resistor_5 (.node(BUS_1));
  assign BUS_1 = AO ? ALU_IN_A : 8'bz;  // Controlled_Buffer controlled_buffer_2
  assign BUS_1 = BO ? ALU_IN_B : 8'bz;  // Controlled_Buffer controlled_buffer_3
  // Switch switch_3: pin names not known; wires that end beside it: 1'b1, switch_3_p2
  Pull_Resistor pull_resistor_6 (.node(switch_3_p2));
  Pull_Resistor pull_resistor_7 (.node(BUS_1));
  assign BUS_1 = switch_3_p2 ? 8'h3 : 8'bz;  // Controlled_Buffer controlled_buffer_4
  Register OUTPUT_REG (.D(BUS_1), .en(OI), .clk(clk), .Q({OUTPUT_REG_q_2, OUTPUT_REG_q}));  // open: clr
  LedBar ledbar_2 (
    .led0(OUTPUT_REG_q_2[3]), .led1(OUTPUT_REG_q_2[2]), .led2(OUTPUT_REG_q_2[1]), .led3(OUTPUT_REG_q_2[0]),
    .led4(OUTPUT_REG_q[3]), .led5(OUTPUT_REG_q[2]), .led6(OUTPUT_REG_q[1]), .led7(OUTPUT_REG_q[0]));
  Register #(.width(4)) MAR (.D(BUS_1[3:0]), .en(MI), .clk(clk), .Q(MAR_q));  // open: clr
  Hex_Digit_Display hex_digit_display_1 (.value(OUTPUT_REG_q_2));  // open: dp
  Hex_Digit_Display hex_digit_display_2 (.value(OUTPUT_REG_q));  // open: dp
  RAM #(.addrWidth(4), .asyncread("true"), .clearpin("true"), .\type ("nonvolatile")) ram_1 (
    .addr(MAR_q), .we(RI), .oe(RO), .clk(clk), .din(controlled_buffer_5_out), .dout(ram_1_dout));  // open: clr
  assign controlled_buffer_5_out = RI ? BUS_1 : 8'bz;  // Controlled_Buffer controlled_buffer_5
  and and_2 (and_2_out, ALO, ADD, ~SUB);  // AND_Gate
  Adder adder_1 (.a(ALU_IN_A), .b(ALU_IN_B), .out(adder_1_out));  // open: cin, cout
  and and_3 (and_3_out, ALO, ~ADD, SUB);  // AND_Gate
  Subtractor subtractor_1 (.a(ALU_IN_A), .b(ALU_IN_B), .out(subtractor_1_out));  // open: bin, bout
  assign BUS_1 = and_2_out ? adder_1_out : 8'bz;  // Controlled_Buffer controlled_buffer_6
  assign BUS_1 = and_3_out ? subtractor_1_out : 8'bz;  // Controlled_Buffer controlled_buffer_7
  assign BUS_1 = RO ? ram_1_dout : 8'bz;  // Controlled_Buffer controlled_buffer_8
  Register #(.width(4)) register_1 (.D(BUS_1[3:0]), .en(II), .clk(clk), .Q(register_1_q));  // open: clr
  assign BUS_1[3:0] = IO ? ~register_1_q : 4'bz;  // Controlled_Inverter controlled_inverter_1
  and and_4 (and_4_out, CE, clk);
  assign controlled_buffer_9_out = JMP ? BUS_1[3:0] : 4'bz;  // Controlled_Buffer controlled_buffer_9
  Counter #(.max('hf), .width(4)) counter_1 (
    .load(JMP), .up(CE), .clk(and_4_out), .D(controlled_buffer_9_out), .Q(counter_1_q));  // open: clr, count, carry
  assign BUS_1[3:0] = CO ? counter_1_q : 4'bz;  // Controlled_Buffer controlled_buffer_10

  // Other names for the same wires on the sheet: BUS_4LSB[3:0] = BUS_1[3:0]
endmodule

module CTRL (
  input  CLK,
  input  [3:0] IR_IN,
  output [23:0] CONTROL_PINS
);

  wire and_1_out, decoder_1_out0, decoder_1_out3, decoder_1_out4, decoder_1_out5, not_1_out, or_1_out;
  wire [2:0] counter_1_q, counter_2_q;

  Pull_Resistor pull_resistor_1 (.node(CONTROL_PINS));
  Counter #(.max('h7), .width(3)) counter_1 (
    .count(1'b1), .Q(counter_1_q), .up(1'b1), .clk(not_1_out), .clr(decoder_1_out5));  // open: load, D, carry
  not not_1 (not_1_out, CLK);
  Decoder #(.select(3)) decoder_1 (
    .out0(decoder_1_out0), .out1(CONTROL_PINS[11]), .out3(decoder_1_out3), .out4(decoder_1_out4),
    .out5(decoder_1_out5), .sel(counter_1_q));  // open: out2, out6, out7, en
  and and_1 (and_1_out, or_1_out, not_1_out);
  or or_1 (or_1_out, decoder_1_out3, decoder_1_out4);
  Counter #(.max('h7), .width(3)) counter_2 (
    .count(1'b1), .Q(counter_2_q), .up(1'b1), .clk(and_1_out), .clr(decoder_1_out5));  // open: load, D, carry
  buf buffer_1 (CONTROL_PINS[8], decoder_1_out0);
  buf buffer_2 (CONTROL_PINS[13], decoder_1_out0);
  buf buffer_3 (CONTROL_PINS[10], CONTROL_PINS[11]);
  buf buffer_4 (CONTROL_PINS[7], CONTROL_PINS[11]);
  ROM #(.addrWidth(7), .dataWidth(24)) rom_1 (.addr({IR_IN, counter_2_q}));  // open: data

  // Other names for the same wires on the sheet: AI = CONTROL_PINS[0]; AO = CONTROL_PINS[1]; BI = CONTROL_PINS[2];
  //   BO = CONTROL_PINS[3]; ALO = CONTROL_PINS[4]; ADD = CONTROL_PINS[5]; SUB = CONTROL_PINS[6]; II = CONTROL_PINS[7];
  //   MI = CONTROL_PINS[8]; RI = CONTROL_PINS[9]; RO = CONTROL_PINS[10]; CE = CONTROL_PINS[11];
  //   JMP = CONTROL_PINS[12]; CO = CONTROL_PINS[13]; OI = CONTROL_PINS[14]; IO = CONTROL_PINS[15]

  // Notes on the sheet:
  //   CONTROL_PINS: pull=down
endmodule
